// Logisim project 12var.circ as structural Verilog: 1 circuit, main circuit main
module main (
  input  B,
  input  C,
  input  G,
  input  H,
  input  I,
  output S
);

  wire xor_1_out, xor_2_out, xor_3_out;

  xor xor_1 (xor_1_out, B, C);
  xor xor_2 (xor_2_out, G, H);
  xor xor_3 (xor_3_out, xor_2_out, I);
  xnor xnor_1 (S, xor_1_out, xor_3_out);
endmodule
