// Logisim project original.circ as structural Verilog: 1 circuit, main circuit main
module main (
  input  A,
  input  B,
  input  C,
  input  D,
  input  E,
  output out_6
);

  wire and_1_out, and_2_out, not_1_out, not_2_out, not_3_out, not_4_out, or_1_out, or_2_out, or_3_out,
       or_4_out, or_5_out, xnor_1_out, xor_1_out, xor_2_out;

  or or_1 (or_1_out, A, B);
  not not_1 (not_1_out, or_1_out);
  or or_2 (or_2_out, A, C);
  or or_3 (or_3_out, A, B, C);
  or or_4 (or_4_out, A, B, D);
  not not_2 (not_2_out, or_4_out);
  or or_5 (or_5_out, A, B);
  and and_1 (and_1_out, not_1_out, or_2_out);
  not not_3 (not_3_out, or_3_out);
  and and_2 (and_2_out, E, or_5_out);
  xor xor_1 (xor_1_out, and_1_out, not_3_out);
  not not_4 (not_4_out, and_2_out);
  xnor xnor_1 (xnor_1_out, xor_1_out, not_2_out);
  xor xor_2 (xor_2_out, xnor_1_out, not_4_out);
endmodule
