// Logisim project simplified.circ as structural Verilog: 1 circuit, main circuit main
module main (
  input  A,
  input  B,
  input  D,
  input  E,
  output out_5
);

  wire and_1_out, not_1_out, not_2_out, not_3_out, not_4_out, or_1_out, or_2_out, xor_1_out;

  not not_1 (not_1_out, A);
  not not_2 (not_2_out, B);
  not not_3 (not_3_out, D);
  not not_4 (not_4_out, E);
  and and_1 (and_1_out, not_1_out, not_2_out);
  or or_1 (or_1_out, A, B, not_3_out);
  or or_2 (or_2_out, and_1_out, not_4_out);
  xor xor_1 (xor_1_out, or_1_out, or_2_out);
endmodule
